// Logisim project circuito-muxes.circ as structural Verilog: 10 circuits, main circuit main
module main (
  input  _0_clock___1_pins,
  input  H,
  input  I,
  input  J,
  input  K,
  input  L,
  input  M
);

  wire bcd_1_a, bcd_1_b, bcd_1_c, bcd_1_d, bcd_1_e, bcd_1_f, bcd_1_g, bcd_2_a, bcd_2_b, bcd_2_c, bcd_2_d,
       bcd_2_e, bcd_2_f, bcd_2_g, w1_1_w1, w2_1_x1, x1_1_x1, x2_1_x2, y1_1_y1, y2_1_y2, z1_1_z1, z2_1_z2;
  wire [5:0] M_out, multiplexer_1_out;

  Clock #(.highDuration(32), .lowDuration(32)) u_H (.out(M_out[5]));
  Clock #(.highDuration(16), .lowDuration(16)) u_I (.out(M_out[4]));
  Clock #(.highDuration(8), .lowDuration(8)) u_J (.out(M_out[3]));
  Clock #(.highDuration(4), .lowDuration(4)) u_K (.out(M_out[2]));
  Clock #(.highDuration(2), .lowDuration(2)) u_L (.out(M_out[1]));
  Clock u_M (.out(M_out[0]));
  Multiplexer #(.width(6), .enable("false")) multiplexer_1 (
    .in0(M_out), .in1({H, I, J, K, L, M}), .out(multiplexer_1_out), .sel(_0_clock___1_pins));
  X1 x1_1 (
    .H(multiplexer_1_out[5]), .I(multiplexer_1_out[4]), .J(multiplexer_1_out[3]), .K(multiplexer_1_out[2]),
    .L(multiplexer_1_out[1]), .M(multiplexer_1_out[0]), .X1(x1_1_x1));
  Y1 y1_1 (
    .H(multiplexer_1_out[5]), .I(multiplexer_1_out[4]), .J(multiplexer_1_out[3]), .K(multiplexer_1_out[2]),
    .L(multiplexer_1_out[1]), .M(multiplexer_1_out[0]), .Y1(y1_1_y1));
  Z1 z1_1 (
    .H(multiplexer_1_out[5]), .I(multiplexer_1_out[4]), .J(multiplexer_1_out[3]), .K(multiplexer_1_out[2]),
    .L(multiplexer_1_out[1]), .M(multiplexer_1_out[0]), .Z1(z1_1_z1));
  W1 w1_1 (
    .H(multiplexer_1_out[5]), .I(multiplexer_1_out[4]), .J(multiplexer_1_out[3]), .K(multiplexer_1_out[2]),
    .L(multiplexer_1_out[1]), .M(multiplexer_1_out[0]), .W1(w1_1_w1));
  bcd bcd_1 (
    .X(x1_1_x1), .Y(y1_1_y1), .Z(z1_1_z1), .W(w1_1_w1), .a(bcd_1_a), .b(bcd_1_b), .c(bcd_1_c), .d(bcd_1_d),
    .e(bcd_1_e), .f(bcd_1_f), .g(bcd_1_g));
  _7_Segment_Display u_7_segment_display_1 (
    .g(bcd_1_g), .f(bcd_1_f), .a(bcd_1_a), .b(bcd_1_b), .e(bcd_1_e), .d(bcd_1_d), .c(bcd_1_c), .dp(1'b1));
  _7_Segment_Display u_7_segment_display_2 (
    .g(bcd_2_g), .f(bcd_2_f), .a(bcd_2_a), .b(bcd_2_b), .e(bcd_2_e), .d(bcd_2_d), .c(bcd_2_c), .dp(1'b1));
  bcd bcd_2 (
    .X(x2_1_x2), .Y(y2_1_y2), .Z(z2_1_z2), .W(w2_1_x1), .a(bcd_2_a), .b(bcd_2_b), .c(bcd_2_c), .d(bcd_2_d),
    .e(bcd_2_e), .f(bcd_2_f), .g(bcd_2_g));
  X2 x2_1 (
    .H(multiplexer_1_out[5]), .I(multiplexer_1_out[4]), .J(multiplexer_1_out[3]), .K(multiplexer_1_out[2]),
    .L(multiplexer_1_out[1]), .M(multiplexer_1_out[0]), .X2(x2_1_x2));
  Y2 y2_1 (
    .H(multiplexer_1_out[5]), .I(multiplexer_1_out[4]), .J(multiplexer_1_out[3]), .K(multiplexer_1_out[2]),
    .L(multiplexer_1_out[1]), .M(multiplexer_1_out[0]), .Y2(y2_1_y2));
  Z2 z2_1 (
    .H(multiplexer_1_out[5]), .I(multiplexer_1_out[4]), .J(multiplexer_1_out[3]), .K(multiplexer_1_out[2]),
    .L(multiplexer_1_out[1]), .M(multiplexer_1_out[0]), .Z2(z2_1_z2));
  W2 w2_1 (
    .H(multiplexer_1_out[5]), .I(multiplexer_1_out[4]), .J(multiplexer_1_out[3]), .K(multiplexer_1_out[2]),
    .L(multiplexer_1_out[1]), .M(multiplexer_1_out[0]), .X1(w2_1_x1));
endmodule

// bcd-7seg
module bcd (
  input  X,
  input  Y,
  input  Z,
  input  W,
  output a,
  output b,
  output c,
  output d,
  output e,
  output f,
  output g
);

  wire and_1_out, and_2_out, and_3_out, and_4_out, and_5_out, and_6_out, and_7_out, and_8_out, and_9_out,
       and_10_out, and_11_out, and_12_out, and_13_out, and_14_out, and_15_out, and_16_out, and_17_out,
       and_18_out, and_19_out, and_20_out, and_21_out, and_22_out, and_23_out, and_24_out, and_25_out,
       and_26_out, and_27_out, not_1_out, not_2_out, not_3_out, not_4_out, not_5_out, not_6_out, not_7_out,
       not_8_out, not_9_out, not_10_out, not_11_out, not_12_out, not_13_out, not_14_out, not_15_out,
       not_16_out, not_17_out, not_18_out, not_19_out, not_20_out, not_21_out, not_22_out, not_23_out,
       not_24_out, not_25_out, not_26_out, not_27_out, not_28_out, not_29_out, not_30_out, not_31_out,
       not_32_out, not_33_out, not_34_out, not_35_out;

  not not_1 (not_1_out, X);
  not not_2 (not_2_out, W);
  not not_3 (not_3_out, Z);
  not not_4 (not_4_out, Y);
  not not_5 (not_5_out, Y);
  not not_6 (not_6_out, W);
  not not_7 (not_7_out, Z);
  not not_8 (not_8_out, X);
  not not_9 (not_9_out, X);
  not not_10 (not_10_out, Z);
  not not_11 (not_11_out, Y);
  not not_12 (not_12_out, Y);
  not not_13 (not_13_out, X);
  not not_14 (not_14_out, Z);
  not not_15 (not_15_out, X);
  not not_16 (not_16_out, W);
  not not_17 (not_17_out, Y);
  not not_18 (not_18_out, Y);
  not not_19 (not_19_out, Z);
  not not_20 (not_20_out, W);
  not not_21 (not_21_out, W);
  not not_22 (not_22_out, W);
  not not_23 (not_23_out, Y);
  not not_24 (not_24_out, W);
  not not_25 (not_25_out, W);
  not not_26 (not_26_out, Z);
  not not_27 (not_27_out, Z);
  not not_28 (not_28_out, W);
  not not_29 (not_29_out, W);
  not not_30 (not_30_out, Y);
  not not_31 (not_31_out, X);
  not not_32 (not_32_out, Z);
  not not_33 (not_33_out, Y);
  not not_34 (not_34_out, Z);
  not not_35 (not_35_out, X);
  and and_1 (and_1_out, W, Y);
  and and_2 (and_2_out, Z, not_1_out);
  and and_3 (and_3_out, W, X);
  and and_4 (and_4_out, not_2_out, not_3_out, not_4_out);
  and and_5 (and_5_out, W, X);
  and and_6 (and_6_out, W, Z);
  and and_7 (and_7_out, not_6_out, not_7_out, not_8_out);
  and and_8 (and_8_out, not_9_out, Y);
  and and_9 (and_9_out, not_10_out, not_11_out);
  and and_10 (and_10_out, not_12_out, X);
  and and_11 (and_11_out, not_13_out, Y, W, not_14_out);
  and and_12 (and_12_out, not_15_out, Z, not_16_out);
  and and_13 (and_13_out, not_17_out, Z, W);
  and and_14 (and_14_out, not_18_out, not_19_out, not_20_out);
  and and_15 (and_15_out, X, Y, not_21_out);
  and and_16 (and_16_out, X, Z);
  and and_17 (and_17_out, Z, not_22_out);
  and and_18 (and_18_out, X, Y);
  and and_19 (and_19_out, not_23_out, not_24_out);
  and and_20 (and_20_out, not_25_out, not_26_out);
  and and_21 (and_21_out, not_27_out, Y);
  and and_22 (and_22_out, not_28_out, Y);
  and and_23 (and_23_out, not_29_out, Z);
  and and_24 (and_24_out, Z, not_30_out, not_31_out);
  and and_25 (and_25_out, W, Y, X);
  and and_26 (and_26_out, not_32_out, not_33_out, X);
  and and_27 (and_27_out, not_34_out, Y, not_35_out);
  or or_1 (a, and_1_out, and_2_out, and_3_out, and_4_out);
  or or_2 (b, not_5_out, and_5_out, and_6_out, and_7_out);
  or or_3 (c, W, and_8_out, and_9_out, and_10_out);
  or or_4 (d, and_11_out, and_12_out, and_13_out, and_14_out, and_15_out);
  or or_5 (e, and_16_out, and_17_out, and_18_out, and_19_out);
  or or_6 (f, and_20_out, and_21_out, and_22_out, X);
  or or_7 (g, and_23_out, and_24_out, and_25_out, and_26_out, and_27_out);
endmodule

module X1 (
  input  H,
  input  I,
  input  J,
  input  K,
  input  L,
  input  M,
  output X1
);

  Multiplexer #(.select(5), .enable("false")) multiplexer_1 (
    .in0(1'b0), .in1(1'b0), .in2(1'b0), .in3(1'b0), .in4(1'b0), .in5(1'b0), .in6(1'b0), .in7(1'b0),
    .in8(1'b0), .in9(1'b0), .in10(1'b0), .in11(1'b0), .in12(1'b0), .in13(1'b0), .in14(1'b0), .in15(1'b0),
    .in16(1'b0), .in17(1'b0), .in18(1'b0), .in19(1'b0), .in20(1'b0), .in21(1'b0), .in22(1'b0), .in23(1'b0),
    .in24(1'b0), .in25(1'b0), .in26(1'b0), .in27(1'b0), .in28(1'b0), .in29(1'b0), .in30(1'b0), .in31(1'b0),
    .out(X1), .sel({M, L, K, J, H}));
endmodule

module Y1 (
  input  H,
  input  I,
  input  J,
  input  K,
  input  L,
  input  M,
  output Y1
);

  Multiplexer #(.select(4), .enable("false")) multiplexer_1 (
    .in0(1'b0), .in1(1'b0), .in2(1'b0), .in3(1'b0), .in4(1'b0), .in5(1'b0), .in6(1'b0), .in7(1'b0), .in8(J),
    .in9(J), .in10(J), .in11(J), .in12(1'b1), .in13(1'b1), .in14(1'b1), .in15(1'b1), .out(Y1),
    .sel({H, I, L, M}));
endmodule

module Z1 (
  input  H,
  input  I,
  input  J,
  input  K,
  input  L,
  input  M,
  output Z1
);

  wire not_1_out, not_2_out, not_3_out, not_4_out;

  not not_1 (not_1_out, H);
  not not_2 (not_2_out, H);
  not not_3 (not_3_out, H);
  not not_4 (not_4_out, H);
  Multiplexer #(.select(4), .enable("false")) multiplexer_1 (
    .in0(H), .in1(H), .in2(H), .in3(H), .in4(1'b0), .in5(1'b0), .in6(1'b0), .in7(1'b0), .in8(1'b0),
    .in9(1'b0), .in10(not_1_out), .in11(not_2_out), .in12(not_3_out), .in13(not_4_out), .in14(1'b1),
    .in15(1'b1), .out(Z1), .sel({I, J, K, L}));
endmodule

module W1 (
  input  H,
  input  I,
  input  J,
  input  K,
  input  L,
  input  M,
  output W1
);

  wire multiplexer_1_out, multiplexer_2_out, multiplexer_3_out, multiplexer_4_out, multiplexer_5_out;

  Multiplexer #(.select(3), .enable("false")) multiplexer_1 (
    .in0(1'b1), .in1(1'b1), .in2(1'b1), .in3(1'b1), .in4(1'b1), .in5(1'b1), .in6(1'b1), .in7(1'b1),
    .out(multiplexer_1_out), .sel({K, L, M}));
  Multiplexer #(.select(3), .enable("false")) multiplexer_2 (
    .in0(1'b1), .in1(1'b1), .in2(1'b1), .in3(1'b1), .in4(1'b0), .in5(1'b0), .in6(1'b0), .in7(1'b0),
    .out(multiplexer_2_out), .sel({K, L, M}));
  Multiplexer #(.select(3), .enable("false")) multiplexer_3 (
    .in0(1'b0), .in1(1'b0), .in2(1'b0), .in3(1'b0), .in4(1'b0), .in5(1'b0), .in6(1'b1), .in7(1'b1),
    .out(multiplexer_3_out), .sel({K, L, M}));
  Multiplexer #(.select(3), .enable("false")) multiplexer_4 (
    .in0(1'b0), .in1(1'b0), .in2(1'b0), .in3(1'b0), .in4(1'b0), .in5(1'b0), .in6(1'b0), .in7(1'b0),
    .out(multiplexer_4_out), .sel({K, L, M}));
  Multiplexer #(.select(3), .enable("false")) multiplexer_5 (
    .in0(1'b0), .in1(1'b0), .in2(1'b1), .in3(1'b1), .in4(1'b1), .in5(1'b1), .in6(1'b1), .in7(1'b1),
    .out(multiplexer_5_out), .sel({K, L, M}));
  Multiplexer #(.select(3), .enable("false")) multiplexer_6 (
    .in0(multiplexer_4_out), .in1(multiplexer_5_out), .in2(multiplexer_2_out), .in3(multiplexer_3_out),
    .in4(multiplexer_1_out), .in5(multiplexer_4_out), .in6(multiplexer_5_out), .in7(multiplexer_2_out),
    .out(W1), .sel({H, I, J}));
endmodule

module X2 (
  input  H,
  input  I,
  input  J,
  input  K,
  input  L,
  input  M,
  output X2
);

  wire multiplexer_1_out, multiplexer_2_out, multiplexer_3_out, multiplexer_4_out, not_1_out;

  not not_1 (not_1_out, L);
  Multiplexer #(.select(2), .enable("false")) multiplexer_1 (
    .in0(L), .in1(1'b0), .in2(1'b0), .in3(not_1_out), .out(multiplexer_1_out), .sel({J, K}));
  Multiplexer #(.select(2), .enable("false")) multiplexer_2 (
    .in0(1'b0), .in1(L), .in2(1'b0), .in3(1'b0), .out(multiplexer_2_out), .sel({J, K}));
  Multiplexer #(.select(2), .enable("false")) multiplexer_3 (
    .in0(not_1_out), .in1(1'b0), .in2(L), .in3(1'b0), .out(multiplexer_3_out), .sel({J, K}));
  Multiplexer #(.select(2), .enable("false")) multiplexer_4 (
    .in0(1'b0), .in1(1'b0), .in2(not_1_out), .in3(1'b0), .out(multiplexer_4_out), .sel({J, K}));
  Multiplexer #(.select(3), .enable("false")) multiplexer_5 (
    .in0(multiplexer_4_out), .in1(multiplexer_4_out), .in2(multiplexer_1_out), .in3(multiplexer_1_out),
    .in4(multiplexer_2_out), .in5(multiplexer_2_out), .in6(multiplexer_3_out), .in7(multiplexer_3_out),
    .out(X2), .sel({H, I, M}));
endmodule

module Y2 (
  input  H,
  input  I,
  input  J,
  input  K,
  input  L,
  input  M,
  output Y2
);

  wire and_1_out, and_2_out, and_3_out, and_4_out, and_5_out, and_6_out, multiplexer_1_out,
       multiplexer_2_out, not_1_out, not_2_out, or_1_out, or_2_out;

  not not_1 (not_1_out, J);
  not not_2 (not_2_out, K);
  and and_1 (and_1_out, not_1_out, K);
  and and_2 (and_2_out, not_2_out, J);
  and and_3 (and_3_out, not_1_out, not_2_out);
  and and_4 (and_4_out, K, J);
  and and_5 (and_5_out, not_1_out, K);
  and and_6 (and_6_out, not_2_out, J);
  or or_1 (or_1_out, and_3_out, and_4_out);
  or or_2 (or_2_out, and_5_out, and_6_out);
  Multiplexer #(.select(2), .enable("false")) multiplexer_1 (
    .in0(K), .in1(and_2_out), .in2(or_1_out), .in3(or_2_out), .out(multiplexer_1_out), .sel({H, I}));
  Multiplexer #(.select(2), .enable("false")) multiplexer_2 (
    .in0(and_1_out), .in1(not_2_out), .in2(K), .in3(and_2_out), .out(multiplexer_2_out), .sel({H, I}));
  Multiplexer #(.select(2), .enable("false")) multiplexer_3 (
    .in0(multiplexer_2_out), .in1(multiplexer_2_out), .in2(multiplexer_1_out), .in3(multiplexer_1_out),
    .out(Y2), .sel({L, M}));
endmodule

module Z2 (
  input  H,
  input  I,
  input  J,
  input  K,
  input  L,
  input  M,
  output Z2
);

  wire multiplexer_1_out, multiplexer_2_out, multiplexer_3_out, multiplexer_4_out, multiplexer_5_out,
       multiplexer_6_out, multiplexer_7_out, multiplexer_8_out, multiplexer_9_out;

  Multiplexer #(.select(2), .enable("false")) multiplexer_1 (
    .in0(1'b0), .in1(1'b1), .in2(1'b0), .in3(1'b0), .out(multiplexer_1_out), .sel({K, L}));
  Multiplexer #(.select(2), .enable("false")) multiplexer_2 (
    .in0(1'b1), .in1(1'b0), .in2(1'b1), .in3(1'b0), .out(multiplexer_2_out), .sel({K, L}));
  Multiplexer #(.select(2), .enable("false")) multiplexer_3 (
    .in0(1'b0), .in1(1'b1), .in2(1'b0), .in3(1'b1), .out(multiplexer_3_out), .sel({K, L}));
  Multiplexer #(.select(2), .enable("false")) multiplexer_4 (
    .in0(1'b0), .in1(1'b0), .in2(1'b1), .in3(1'b0), .out(multiplexer_4_out), .sel({K, L}));
  Multiplexer #(.select(2), .enable("false")) multiplexer_5 (
    .in0(1'b1), .in1(1'b0), .in2(1'b0), .in3(1'b1), .out(multiplexer_5_out), .sel({K, L}));
  Multiplexer #(.enable("false")) multiplexer_6 (
    .in0(multiplexer_2_out), .in1(multiplexer_3_out), .out(multiplexer_6_out), .sel(J));
  Multiplexer #(.enable("false")) multiplexer_7 (
    .in0(multiplexer_4_out), .in1(multiplexer_5_out), .out(multiplexer_7_out), .sel(J));
  Multiplexer #(.enable("false")) multiplexer_8 (
    .in0(multiplexer_3_out), .in1(multiplexer_4_out), .out(multiplexer_8_out), .sel(J));
  Multiplexer #(.enable("false")) multiplexer_9 (
    .in0(multiplexer_5_out), .in1(multiplexer_1_out), .out(multiplexer_9_out), .sel(J));
  Multiplexer #(.select(2), .enable("false")) multiplexer_10 (
    .in0(multiplexer_8_out), .in1(multiplexer_9_out), .in2(multiplexer_6_out), .in3(multiplexer_7_out),
    .out(Z2), .sel({H, I}));
endmodule

module W2 (
  input  H,
  input  I,
  input  J,
  input  K,
  input  L,
  input  M,
  output X1
);

  Multiplexer #(.select(5), .enable("false")) multiplexer_1 (
    .in0(1'b0), .in1(1'b0), .in2(1'b0), .in3(1'b0), .in4(1'b0), .in5(1'b0), .in6(1'b0), .in7(1'b0),
    .in8(1'b0), .in9(1'b0), .in10(1'b0), .in11(1'b0), .in12(1'b0), .in13(1'b0), .in14(1'b0), .in15(1'b0),
    .in16(1'b0), .in17(1'b0), .in18(1'b0), .in19(1'b0), .in20(1'b0), .in21(1'b0), .in22(1'b0), .in23(1'b0),
    .in24(1'b0), .in25(1'b0), .in26(1'b0), .in27(1'b0), .in28(1'b0), .in29(1'b0), .in30(1'b0), .in31(1'b0),
    .out(X1), .sel({M, L, K, J, H}));
endmodule
