// Logisim project 6bit2bcd.circ as structural Verilog: 10 circuits, main circuit main
module main (
  input  [5:0] in_1,
  output [3:0] MSB_top,
  output [3:0] LSB_top,
  output [2:0] MSB_bot,
  output [2:0] LSB_bot
);

  wire a0_6bit_bcd_1_a0, a1_6bit_bcd_1_a1, b0_6bit_bcd_1_b0, b1_6bit_bcd_1_b1, c0_6bit_bcd_1_c0,
       c1_6bit_bcd_1_c1, d0_6bit_bcd_1_d0, d1_6bit_bcd_1_d1;

  A1_6bit_bcd a1_6bit_bcd_1 (.in_1(in_1), .A1(a1_6bit_bcd_1_a1));
  B1_6bit_bcd b1_6bit_bcd_1 (.in_1(in_1), .B1(b1_6bit_bcd_1_b1));
  C1_6bit_bcd c1_6bit_bcd_1 (.in_1(in_1), .C1(c1_6bit_bcd_1_c1));
  D1_6bit_bcd d1_6bit_bcd_1 (.in_1(in_1), .D1(d1_6bit_bcd_1_d1));
  _7_Segment_Display u_7_segment_display_1 (
    .g(MSB_top[0]), .f(MSB_top[1]), .a(MSB_top[2]), .b(MSB_top[3]), .e(MSB_bot[2]), .d(MSB_bot[1]),
    .c(MSB_bot[0]));  // open: dp
  bcd_7seg bcd_7seg_1 (
    .A(a1_6bit_bcd_1_a1), .B(b1_6bit_bcd_1_b1), .C(c1_6bit_bcd_1_c1), .D(d1_6bit_bcd_1_d1), .a_2(MSB_top[2]),
    .b_2(MSB_top[3]), .c_2(MSB_bot[0]), .d_2(MSB_bot[1]), .e(MSB_bot[2]), .f(MSB_top[1]), .g(MSB_top[0]));
  A0_6bit_bcd a0_6bit_bcd_1 (.in_1(in_1), .A0(a0_6bit_bcd_1_a0));
  B0_6bit_bcd b0_6bit_bcd_1 (.in_1(in_1), .B0(b0_6bit_bcd_1_b0));
  C0_6bit_bcd c0_6bit_bcd_1 (.in_1(in_1), .C0(c0_6bit_bcd_1_c0));
  D0_6bit_bcd d0_6bit_bcd_1 (.in_1(in_1), .D0(d0_6bit_bcd_1_d0));
  _7_Segment_Display u_7_segment_display_2 (
    .g(LSB_top[0]), .f(LSB_top[1]), .a(LSB_top[2]), .b(LSB_top[3]), .e(LSB_bot[2]), .d(LSB_bot[1]),
    .c(LSB_bot[0]));  // open: dp
  bcd_7seg bcd_7seg_2 (
    .A(a0_6bit_bcd_1_a0), .B(b0_6bit_bcd_1_b0), .C(c0_6bit_bcd_1_c0), .D(d0_6bit_bcd_1_d0), .a_2(LSB_top[2]),
    .b_2(LSB_top[3]), .c_2(LSB_bot[0]), .d_2(LSB_bot[1]), .e(LSB_bot[2]), .f(LSB_top[1]), .g(LSB_top[0]));
endmodule

module bcd_7seg (
  input  A,
  input  B,
  input  C,
  input  D,
  output a_2,
  output b_2,
  output c_2,
  output d_2,
  output e,
  output f,
  output g
);

  wire and_1_out, and_2_out, and_3_out, and_4_out, and_5_out, and_6_out, and_7_out, and_8_out, and_9_out,
       and_10_out, and_11_out, and_12_out, and_13_out, and_14_out, and_15_out, and_16_out, and_17_out,
       and_18_out, and_19_out, and_20_out, and_21_out, and_22_out, and_23_out, and_24_out, and_25_out,
       and_26_out, and_27_out, not_1_out, not_2_out, not_3_out, not_4_out, not_5_out, not_6_out, not_7_out,
       not_8_out, not_9_out, not_10_out, not_11_out, not_12_out, not_13_out, not_14_out, not_15_out,
       not_16_out, not_17_out, not_18_out, not_19_out, not_20_out, not_21_out, not_22_out, not_23_out,
       not_24_out, not_25_out, not_26_out, not_27_out, not_28_out, not_29_out, not_30_out, not_31_out,
       not_32_out, not_33_out, not_34_out, not_35_out;

  and and_1 (and_1_out, D, B);
  and and_2 (and_2_out, C, not_1_out);
  not not_1 (not_1_out, A);
  and and_3 (and_3_out, D, A);
  not not_2 (not_2_out, D);
  and and_4 (and_4_out, not_2_out, not_3_out, not_4_out);
  not not_3 (not_3_out, C);
  not not_4 (not_4_out, B);
  not not_5 (not_5_out, B);
  and and_5 (and_5_out, D, A);
  and and_6 (and_6_out, D, C);
  not not_6 (not_6_out, D);
  and and_7 (and_7_out, not_6_out, not_7_out, not_8_out);
  not not_7 (not_7_out, C);
  not not_8 (not_8_out, A);
  not not_9 (not_9_out, A);
  and and_8 (and_8_out, not_9_out, B);
  not not_10 (not_10_out, C);
  and and_9 (and_9_out, not_10_out, not_11_out);
  not not_11 (not_11_out, B);
  not not_12 (not_12_out, B);
  and and_10 (and_10_out, not_12_out, A);
  not not_13 (not_13_out, A);
  and and_11 (and_11_out, not_13_out, B, D, not_14_out);
  not not_14 (not_14_out, C);
  not not_15 (not_15_out, A);
  and and_12 (and_12_out, not_15_out, C, not_16_out);
  not not_16 (not_16_out, D);
  not not_17 (not_17_out, B);
  and and_13 (and_13_out, not_17_out, C, D);
  not not_18 (not_18_out, B);
  not not_19 (not_19_out, C);
  and and_14 (and_14_out, not_18_out, not_19_out, not_20_out);
  not not_20 (not_20_out, D);
  and and_15 (and_15_out, A, B, not_21_out);
  not not_21 (not_21_out, D);
  and and_16 (and_16_out, A, C);
  and and_17 (and_17_out, C, not_22_out);
  not not_22 (not_22_out, D);
  and and_18 (and_18_out, A, B);
  not not_23 (not_23_out, B);
  and and_19 (and_19_out, not_23_out, not_24_out);
  not not_24 (not_24_out, D);
  not not_25 (not_25_out, D);
  and and_20 (and_20_out, not_25_out, not_26_out);
  not not_26 (not_26_out, C);
  not not_27 (not_27_out, C);
  and and_21 (and_21_out, not_27_out, B);
  not not_28 (not_28_out, D);
  and and_22 (and_22_out, not_28_out, B);
  not not_29 (not_29_out, D);
  and and_23 (and_23_out, not_29_out, C);
  and and_24 (and_24_out, C, not_30_out, not_31_out);
  not not_30 (not_30_out, B);
  not not_31 (not_31_out, A);
  and and_25 (and_25_out, D, B, A);
  not not_32 (not_32_out, C);
  not not_33 (not_33_out, B);
  and and_26 (and_26_out, not_32_out, not_33_out, A);
  not not_34 (not_34_out, C);
  and and_27 (and_27_out, not_34_out, B, not_35_out);
  not not_35 (not_35_out, A);
  or or_1 (a_2, and_1_out, and_2_out, and_3_out, and_4_out);
  or or_2 (b_2, not_5_out, and_5_out, and_6_out, and_7_out);
  or or_3 (c_2, D, and_8_out, and_9_out, and_10_out);
  or or_4 (d_2, and_11_out, and_12_out, and_13_out, and_14_out, and_15_out);
  or or_5 (e, and_16_out, and_17_out, and_18_out, and_19_out);
  or or_6 (f, and_20_out, and_21_out, and_22_out, A);
  or or_7 (g, and_23_out, and_24_out, and_25_out, and_26_out, and_27_out);
endmodule

// A1
module A1_6bit_bcd (
  input  [5:0] in_1,
  output A1
);

  Multiplexer #(.select(5), .enable("false")) multiplexer_1 (
    .in0(1'b0), .in1(1'b0), .in2(1'b0), .in3(1'b0), .in4(1'b0), .in5(1'b0), .in6(1'b0), .in7(1'b0),
    .in8(1'b0), .in9(1'b0), .in10(1'b0), .in11(1'b0), .in12(1'b0), .in13(1'b0), .in14(1'b0), .in15(1'b0),
    .in16(1'b0), .in17(1'b0), .in18(1'b0), .in19(1'b0), .in20(1'b0), .in21(1'b0), .in22(1'b0), .in23(1'b0),
    .in24(1'b0), .in25(1'b0), .in26(1'b0), .in27(1'b0), .in28(1'b0), .in29(1'b0), .in30(1'b0), .in31(1'b0),
    .out(A1), .sel({in_1[5:2], in_1[0]}));
endmodule

// B1
module B1_6bit_bcd (
  input  [5:0] in_1,
  output B1
);

  Multiplexer #(.select(4), .enable("false")) multiplexer_1 (
    .in0(1'b0), .in1(1'b0), .in2(1'b0), .in3(1'b0), .in4(1'b0), .in5(1'b0), .in6(1'b0), .in7(1'b0),
    .in8(in_1[3]), .in9(in_1[3]), .in10(in_1[3]), .in11(in_1[3]), .in12(1'b1), .in13(1'b1), .in14(1'b1),
    .in15(1'b1), .out(B1), .sel({in_1[5:4], in_1[1:0]}));
endmodule

// C1
module C1_6bit_bcd (
  input  [5:0] in_1,
  output C1
);

  wire not_1_out, not_2_out, not_3_out, not_4_out;

  not not_1 (not_1_out, in_1[5]);
  not not_2 (not_2_out, in_1[5]);
  not not_3 (not_3_out, in_1[5]);
  not not_4 (not_4_out, in_1[5]);
  Multiplexer #(.select(4), .enable("false")) multiplexer_1 (
    .in0(in_1[5]), .in1(in_1[5]), .in2(in_1[5]), .in3(in_1[5]), .in4(1'b0), .in5(1'b0), .in6(1'b0),
    .in7(1'b0), .in8(1'b0), .in9(1'b0), .in10(not_1_out), .in11(not_2_out), .in12(not_3_out),
    .in13(not_4_out), .in14(1'b1), .in15(1'b1), .out(C1), .sel(in_1[4:1]));
endmodule

// D1
module D1_6bit_bcd (
  input  [5:0] in_1,
  output D1
);

  wire multiplexer_1_out, multiplexer_2_out, multiplexer_3_out, multiplexer_4_out, multiplexer_5_out;

  Multiplexer #(.select(3), .enable("false")) multiplexer_1 (
    .in0(1'b1), .in1(1'b1), .in2(1'b1), .in3(1'b1), .in4(1'b0), .in5(1'b0), .in6(1'b0), .in7(1'b0),
    .out(multiplexer_1_out), .sel(in_1[2:0]));
  Multiplexer #(.select(3), .enable("false")) multiplexer_2 (
    .in0(1'b0), .in1(1'b0), .in2(1'b0), .in3(1'b0), .in4(1'b0), .in5(1'b0), .in6(1'b1), .in7(1'b1),
    .out(multiplexer_2_out), .sel(in_1[2:0]));
  Multiplexer #(.select(3), .enable("false")) multiplexer_3 (
    .in0(1'b0), .in1(1'b0), .in2(1'b1), .in3(1'b1), .in4(1'b1), .in5(1'b1), .in6(1'b1), .in7(1'b1),
    .out(multiplexer_3_out), .sel(in_1[2:0]));
  Multiplexer #(.select(3), .enable("false")) multiplexer_4 (
    .in0(1'b1), .in1(1'b1), .in2(1'b1), .in3(1'b1), .in4(1'b1), .in5(1'b1), .in6(1'b1), .in7(1'b1),
    .out(multiplexer_4_out), .sel(in_1[2:0]));
  Multiplexer #(.select(3), .enable("false")) multiplexer_5 (
    .in0(1'b0), .in1(1'b0), .in2(1'b0), .in3(1'b0), .in4(1'b0), .in5(1'b0), .in6(1'b0), .in7(1'b0),
    .out(multiplexer_5_out), .sel(in_1[2:0]));
  Multiplexer #(.select(3), .enable("false")) multiplexer_6 (
    .in0(multiplexer_5_out), .in1(multiplexer_3_out), .in2(multiplexer_1_out), .in3(multiplexer_2_out),
    .in4(multiplexer_4_out), .in5(multiplexer_5_out), .in6(multiplexer_3_out), .in7(multiplexer_1_out),
    .out(D1), .sel(in_1[5:3]));
endmodule

// A0
module A0_6bit_bcd (
  input  [5:0] in_1,
  output A0
);

  wire multiplexer_1_out, multiplexer_2_out, multiplexer_3_out, multiplexer_4_out, not_1_out;

  not not_1 (not_1_out, in_1[1]);
  Multiplexer #(.select(2), .enable("false")) multiplexer_1 (
    .in0(1'b0), .in1(in_1[1]), .in2(1'b0), .in3(1'b0), .out(multiplexer_1_out), .sel(in_1[3:2]));
  Multiplexer #(.select(2), .enable("false")) multiplexer_2 (
    .in0(not_1_out), .in1(1'b0), .in2(in_1[1]), .in3(1'b0), .out(multiplexer_2_out), .sel(in_1[3:2]));
  Multiplexer #(.select(2), .enable("false")) multiplexer_3 (
    .in0(1'b0), .in1(1'b0), .in2(not_1_out), .in3(1'b0), .out(multiplexer_3_out), .sel(in_1[3:2]));
  Multiplexer #(.select(2), .enable("false")) multiplexer_4 (
    .in0(in_1[1]), .in1(1'b0), .in2(1'b0), .in3(not_1_out), .out(multiplexer_4_out), .sel(in_1[3:2]));
  Multiplexer #(.select(3), .enable("false")) multiplexer_5 (
    .in0(multiplexer_3_out), .in1(multiplexer_3_out), .in2(multiplexer_4_out), .in3(multiplexer_4_out),
    .in4(multiplexer_1_out), .in5(multiplexer_1_out), .in6(multiplexer_2_out), .in7(multiplexer_2_out),
    .out(A0), .sel({in_1[5:4], in_1[0]}));
endmodule

// B0
module B0_6bit_bcd (
  input  [5:0] in_1,
  output B0
);

  wire and_1_out, and_2_out, multiplexer_1_out, multiplexer_2_out, not_1_out, not_2_out, xor_1_out;

  not not_1 (not_1_out, in_1[3]);
  not not_2 (not_2_out, in_1[2]);
  and and_1 (and_1_out, not_1_out, in_1[2]);
  and and_2 (and_2_out, not_2_out, in_1[3]);
  xor xor_1 (xor_1_out, not_2_out, in_1[3]);
  Multiplexer #(.select(2), .enable("false")) multiplexer_1 (
    .in0(and_1_out), .in1(not_2_out), .in2(in_1[2]), .in3(and_2_out), .out(multiplexer_1_out), .sel(in_1[5:4]));
  Multiplexer #(.select(2), .enable("false")) multiplexer_2 (
    .in0(in_1[2]), .in1(and_2_out), .in2(xor_1_out), .in3(and_1_out), .out(multiplexer_2_out), .sel(in_1[5:4]));
  Multiplexer #(.select(2), .enable("false")) multiplexer_3 (
    .in0(multiplexer_1_out), .in1(multiplexer_1_out), .in2(multiplexer_2_out), .in3(multiplexer_2_out),
    .out(B0), .sel(in_1[1:0]));
endmodule

// C0
module C0_6bit_bcd (
  input  [5:0] in_1,
  output C0
);

  wire multiplexer_1_out, multiplexer_2_out, multiplexer_3_out, multiplexer_4_out, multiplexer_5_out,
       multiplexer_6_out, multiplexer_7_out, multiplexer_8_out, multiplexer_9_out;

  Multiplexer #(.select(2), .enable("false")) multiplexer_1 (
    .in0(1'b1), .in1(1'b0), .in2(1'b0), .in3(1'b1), .out(multiplexer_1_out), .sel(in_1[2:1]));
  Multiplexer #(.select(2), .enable("false")) multiplexer_2 (
    .in0(1'b0), .in1(1'b1), .in2(1'b0), .in3(1'b0), .out(multiplexer_2_out), .sel(in_1[2:1]));
  Multiplexer #(.select(2), .enable("false")) multiplexer_3 (
    .in0(1'b1), .in1(1'b0), .in2(1'b1), .in3(1'b0), .out(multiplexer_3_out), .sel(in_1[2:1]));
  Multiplexer #(.select(2), .enable("false")) multiplexer_4 (
    .in0(1'b0), .in1(1'b1), .in2(1'b0), .in3(1'b1), .out(multiplexer_4_out), .sel(in_1[2:1]));
  Multiplexer #(.select(2), .enable("false")) multiplexer_5 (
    .in0(1'b0), .in1(1'b0), .in2(1'b1), .in3(1'b0), .out(multiplexer_5_out), .sel(in_1[2:1]));
  Multiplexer #(.enable("false")) multiplexer_6 (
    .in0(multiplexer_5_out), .in1(multiplexer_1_out), .out(multiplexer_6_out), .sel(in_1[3]));
  Multiplexer #(.enable("false")) multiplexer_7 (
    .in0(multiplexer_4_out), .in1(multiplexer_5_out), .out(multiplexer_7_out), .sel(in_1[3]));
  Multiplexer #(.enable("false")) multiplexer_8 (
    .in0(multiplexer_1_out), .in1(multiplexer_2_out), .out(multiplexer_8_out), .sel(in_1[3]));
  Multiplexer #(.enable("false")) multiplexer_9 (
    .in0(multiplexer_3_out), .in1(multiplexer_4_out), .out(multiplexer_9_out), .sel(in_1[3]));
  Multiplexer #(.select(2), .enable("false")) multiplexer_10 (
    .in0(multiplexer_7_out), .in1(multiplexer_8_out), .in2(multiplexer_9_out), .in3(multiplexer_6_out),
    .out(C0), .sel(in_1[5:4]));
endmodule

// D0
module D0_6bit_bcd (
  input  [5:0] in_1,
  output D0
);

  wire multiplexer_1_out, multiplexer_2_out;

  Multiplexer #(.select(2), .enable("false")) multiplexer_1 (
    .in0(1'b0), .in1(1'b1), .in2(1'b0), .in3(1'b1), .out(multiplexer_1_out), .sel(in_1[1:0]));
  Multiplexer #(.select(2), .enable("false")) multiplexer_2 (
    .in0(multiplexer_1_out), .in1(multiplexer_1_out), .in2(multiplexer_1_out), .in3(multiplexer_1_out),
    .out(multiplexer_2_out), .sel(in_1[3:2]));
  Multiplexer #(.select(2), .enable("false")) multiplexer_3 (
    .in0(multiplexer_2_out), .in1(multiplexer_2_out), .in2(multiplexer_2_out), .in3(multiplexer_2_out),
    .out(D0), .sel(in_1[5:4]));
endmodule
