// Logisim project contador.circ as structural Verilog: 5 circuits, main circuit main
module main (
  input  CLK,
  input  EN,
  input  SET,
  input  RESET,
  input  M,
  input  LOAD,
  input  N,
  input  O,
  input  MODE,
  input  P,
  input  Q,
  input  R,
  output [5:0] num,
  output [3:0] LSB_top,
  output [3:0] MSB_top,
  output [2:0] MSB_bot,
  output [2:0] LSB_bot,
  output MAX,
  output ZERO
);

  wire [5:0] multiplexer_1_out, multiplexer_2_out, previo_1_out, siguiente_1_out;

  Multiplexer #(.width(6), .enable("false")) multiplexer_1 (
    .in0(multiplexer_2_out), .in1({M, N, O, P, Q, R}), .out(multiplexer_1_out), .sel(LOAD));
  previo previo_1 (.IN(num), .OUT(previo_1_out));
  Multiplexer #(.width(6), .enable("false")) multiplexer_2 (
    .in0(previo_1_out), .in1(siguiente_1_out), .out(multiplexer_2_out), .sel(MODE));
  siguiente siguiente_1 (.IN(num), .OUT(siguiente_1_out));
  _6bit2bcd_main _6bit2bcd (.in_1(num), .MSB_top(MSB_top), .LSB_top(LSB_top), .MSB_bot(MSB_bot), .LSB_bot(LSB_bot));
  estado estado_1 (.CLK(CLK), .D(multiplexer_1_out), .S(SET), .EN(EN), .R(RESET), .out_6(num));
  zero_max zero_max_1 (.in_1(num), .MAX(MAX), .ZERO(ZERO));
  _7_Segment_Display u_7_segment_display_1 (
    .g(MSB_top[0]), .f(MSB_top[1]), .a(MSB_top[2]), .b(MSB_top[3]), .e(MSB_bot[2]), .d(MSB_bot[1]),
    .c(MSB_bot[0]));  // open: dp
  _7_Segment_Display u_7_segment_display_2 (
    .g(LSB_top[0]), .f(LSB_top[1]), .a(LSB_top[2]), .b(LSB_top[3]), .e(LSB_bot[2]), .d(LSB_bot[1]),
    .c(LSB_bot[0]));  // open: dp
endmodule

module estado (
  input  CLK,
  input  [5:0] D,
  input  S,
  input  EN,
  input  R,
  output [5:0] out_6
);

  D_Flip_Flop d_ff_1 (.clk(CLK), .D(D[5]), .Q(out_6[5]), .preset(S), .en(EN), .reset(R));  // open: Qn
  D_Flip_Flop d_ff_2 (.clk(CLK), .D(D[4]), .Q(out_6[4]), .preset(S), .en(EN), .reset(R));  // open: Qn
  D_Flip_Flop d_ff_3 (.clk(CLK), .D(D[3]), .Q(out_6[3]), .preset(S), .en(EN), .reset(R));  // open: Qn
  D_Flip_Flop d_ff_4 (.clk(CLK), .D(D[2]), .Q(out_6[2]), .preset(S), .en(EN), .reset(R));  // open: Qn
  D_Flip_Flop d_ff_5 (.clk(CLK), .D(D[1]), .Q(out_6[1]), .preset(S), .en(EN), .reset(R));  // open: Qn
  D_Flip_Flop d_ff_6 (.clk(CLK), .D(D[0]), .Q(out_6[0]), .preset(S), .en(EN), .reset(R));  // open: Qn
endmodule

module zero_max (
  input  [5:0] in_1,
  output MAX,
  output ZERO
);

  and and_1 (MAX, in_1[5], in_1[4], in_1[3], in_1[2], in_1[1], in_1[0]);
  nor nor_1 (ZERO, in_1[5], in_1[4], in_1[3], in_1[2], in_1[1], in_1[0]);
endmodule

// +1
module siguiente (
  input  [5:0] IN,
  output [5:0] OUT
);

  wire and_1_out, and_2_out, and_3_out, and_4_out, and_5_out, and_6_out, and_7_out, and_8_out, and_9_out,
       and_10_out, and_11_out, and_12_out, and_13_out, and_14_out, and_15_out, and_16_out, and_17_out,
       and_18_out, not_1_out, not_2_out, not_3_out, not_4_out, not_5_out;

  not not_1 (not_1_out, IN[5]);
  not not_2 (not_2_out, IN[4]);
  not not_3 (not_3_out, IN[3]);
  not not_4 (not_4_out, IN[2]);
  not not_5 (not_5_out, IN[1]);
  not not_6 (OUT[0], IN[0]);
  and and_1 (and_1_out, not_4_out, IN[1], IN[0]);
  and and_2 (and_2_out, IN[2], not_5_out);
  and and_3 (and_3_out, IN[2], OUT[0]);
  and and_4 (and_4_out, not_3_out, IN[2], IN[1], IN[0]);
  and and_5 (and_5_out, IN[3], not_4_out);
  and and_6 (and_6_out, IN[3], not_5_out);
  and and_7 (and_7_out, IN[3], OUT[0]);
  and and_8 (and_8_out, not_2_out, IN[3], IN[2], IN[1], IN[0]);
  and and_9 (and_9_out, IN[4], not_3_out);
  and and_10 (and_10_out, IN[4], not_4_out);
  and and_11 (and_11_out, IN[4], not_5_out);
  and and_12 (and_12_out, IN[4], OUT[0]);
  and and_13 (and_13_out, not_1_out, IN[4], IN[3], IN[2], IN[1], IN[0]);
  and and_14 (and_14_out, IN[5], not_2_out);
  and and_15 (and_15_out, IN[5], not_3_out);
  and and_16 (and_16_out, IN[5], not_4_out);
  and and_17 (and_17_out, IN[5], not_5_out);
  and and_18 (and_18_out, IN[5], OUT[0]);
  xor xor_1 (OUT[1], IN[1], IN[0]);
  or or_1 (OUT[2], and_1_out, and_2_out, and_3_out);
  or or_2 (OUT[3], and_4_out, and_5_out, and_6_out, and_7_out);
  or or_3 (OUT[4], and_8_out, and_9_out, and_10_out, and_11_out, and_12_out);
  or or_4 (OUT[5], and_13_out, and_14_out, and_15_out, and_16_out, and_17_out, and_18_out);
endmodule

// -1
module previo (
  input  [5:0] IN,
  output [5:0] OUT
);

  wire and_1_out, and_2_out, and_3_out, and_4_out, and_5_out, and_6_out, and_7_out, and_8_out, and_9_out,
       and_10_out, and_11_out, and_12_out, and_13_out, and_14_out, and_15_out, and_16_out, and_17_out,
       and_18_out, not_1_out, not_2_out, not_3_out, not_4_out, not_5_out;

  not not_1 (not_1_out, IN[5]);
  not not_2 (not_2_out, IN[4]);
  not not_3 (not_3_out, IN[3]);
  not not_4 (not_4_out, IN[2]);
  not not_5 (not_5_out, IN[1]);
  not not_6 (OUT[0], IN[0]);
  xor xor_1 (OUT[1], not_5_out, IN[0]);
  and and_1 (and_1_out, not_4_out, not_5_out, OUT[0]);
  and and_2 (and_2_out, IN[2], IN[0]);
  or or_1 (OUT[2], and_1_out, and_2_out, and_3_out);
  and and_3 (and_3_out, IN[2], IN[1]);
  and and_4 (and_4_out, not_3_out, not_4_out, not_5_out, OUT[0]);
  and and_5 (and_5_out, IN[3], IN[0]);
  or or_2 (OUT[3], and_4_out, and_5_out, and_6_out, and_7_out);
  and and_6 (and_6_out, IN[3], IN[1]);
  and and_7 (and_7_out, IN[3], IN[2]);
  and and_8 (and_8_out, not_2_out, not_3_out, not_4_out, not_5_out, OUT[0]);
  and and_9 (and_9_out, IN[4], IN[0]);
  and and_10 (and_10_out, IN[4], IN[1]);
  and and_11 (and_11_out, IN[4], IN[2]);
  and and_12 (and_12_out, IN[4], IN[3]);
  and and_13 (and_13_out, not_1_out, not_2_out, not_3_out, not_4_out, not_5_out, OUT[0]);
  and and_14 (and_14_out, IN[5], IN[4]);
  and and_15 (and_15_out, IN[5], IN[3]);
  and and_16 (and_16_out, IN[5], IN[2]);
  and and_17 (and_17_out, IN[5], IN[1]);
  and and_18 (and_18_out, IN[5], IN[0]);
  or or_3 (OUT[4], and_8_out, and_9_out, and_10_out, and_11_out, and_12_out);
  or or_4 (OUT[5], and_13_out, and_14_out, and_15_out, and_16_out, and_17_out, and_18_out);
endmodule
