// Logisim project semaforo.circ as structural Verilog: 5 circuits, main circuit main
module main (
  input  RES
);

  wire CLK_out, decodificador_de_salidas_1_lav, decodificador_de_salidas_1_lrp,
       decodificador_de_salidas_1_lrv, decodificador_de_salidas_1_lvv, maquina_de_estados_1_load,
       maquina_de_estados_1_s0, maquina_de_estados_1_s1, maquina_de_estados_1_se, maquina_de_estados_1_ts,
       modulo_de_tiempos_1_zero, not_1_out, solicitud_de_paso_1_sp_prime, SP_out;
  wire [2:0] modulo_de_tiempos_1_lsb_bot, modulo_de_tiempos_1_msb_bot, multiplexer_3_out, multiplexer_4_out;
  wire [3:0] modulo_de_tiempos_1_lsb_top, modulo_de_tiempos_1_msb_top, multiplexer_1_out, multiplexer_2_out;

  Clock CLK (.out(CLK_out));
  Button SP (.out(SP_out));
  Solicitud_de_Paso solicitud_de_paso_1 (
    .SP(SP_out), .CLK(CLK_out), .RES(RES), .LVP(RES), .SP_prime(solicitud_de_paso_1_sp_prime));
  Maquina_de_Estados maquina_de_estados_1 (
    .CLK(CLK_out), .ZERO(solicitud_de_paso_1_sp_prime), .SP_prime(modulo_de_tiempos_1_zero),
    .S1(maquina_de_estados_1_s1), .S0(maquina_de_estados_1_s0), .SE(maquina_de_estados_1_se),
    .LOAD(maquina_de_estados_1_load), .TS(maquina_de_estados_1_ts));
  Decodificador_de_Salidas decodificador_de_salidas_1 (
    .S1(maquina_de_estados_1_s1), .S0(maquina_de_estados_1_s0), .LRV(decodificador_de_salidas_1_lrv),
    .LAV(decodificador_de_salidas_1_lav), .LVV(decodificador_de_salidas_1_lvv),
    .LRP(decodificador_de_salidas_1_lrp), .LVP(RES));
  not not_1 (not_1_out, maquina_de_estados_1_se);
  Modulo_de_Tiempos modulo_de_tiempos_1 (
    .RESET(RES), .CLK(CLK_out), .LOAD(maquina_de_estados_1_load), .TS(maquina_de_estados_1_ts),
    .MSB_top(modulo_de_tiempos_1_msb_top), .LSB_top(modulo_de_tiempos_1_lsb_top),
    .MSB_bot(modulo_de_tiempos_1_msb_bot), .LSB_bot(modulo_de_tiempos_1_lsb_bot),
    .ZERO(modulo_de_tiempos_1_zero));  // open: SET, EN
  LED LRV (.in(decodificador_de_salidas_1_lrv));
  LED LAV (.in(decodificador_de_salidas_1_lav));
  LED LVV (.in(decodificador_de_salidas_1_lvv));
  LED LRP (.in(decodificador_de_salidas_1_lrp));
  LED LVP (.in(RES));
  Multiplexer #(.width(4), .enable("false")) multiplexer_1 (
    .in0(modulo_de_tiempos_1_msb_top), .in1(4'b0000), .out(multiplexer_1_out), .sel(not_1_out));
  Multiplexer #(.width(4), .enable("false")) multiplexer_2 (
    .in0(modulo_de_tiempos_1_lsb_top), .in1(4'b0000), .out(multiplexer_2_out), .sel(not_1_out));
  Multiplexer #(.width(3), .enable("false")) multiplexer_3 (
    .in0(modulo_de_tiempos_1_msb_bot), .in1(3'b000), .out(multiplexer_3_out), .sel(not_1_out));
  Multiplexer #(.width(3), .enable("false")) multiplexer_4 (
    .in0(modulo_de_tiempos_1_lsb_bot), .in1(3'b000), .out(multiplexer_4_out), .sel(not_1_out));
  _7_Segment_Display u_7_segment_display_1 (
    .g(multiplexer_2_out[0]), .f(multiplexer_2_out[1]), .a(multiplexer_2_out[2]), .b(multiplexer_2_out[3]),
    .e(multiplexer_4_out[2]), .d(multiplexer_4_out[1]), .c(multiplexer_4_out[0]));  // open: dp
  _7_Segment_Display u_7_segment_display_2 (
    .g(multiplexer_1_out[0]), .f(multiplexer_1_out[1]), .a(multiplexer_1_out[2]), .b(multiplexer_1_out[3]),
    .e(multiplexer_3_out[2]), .d(multiplexer_3_out[1]), .c(multiplexer_3_out[0]));  // open: dp
endmodule

module Maquina_de_Estados (
  input  CLK,
  input  ZERO,
  input  SP_prime,
  output S1,
  output S0,
  output SE,
  output LOAD,
  output TS
);

  wire and_1_out, and_2_out, and_3_out, and_4_out, and_5_out, and_6_out, and_7_out, not_1_out, or_1_out,
       or_2_out, or_3_out, Z_q;

  and and_1 (and_1_out, S0, Z_q, ZERO);
  and and_2 (and_2_out, S1, Z_q, ZERO);
  or or_1 (or_1_out, and_2_out, and_3_out);
  and and_3 (and_3_out, S1, ZERO, SP_prime);
  and and_4 (and_4_out, Z_q, ZERO);
  or or_2 (or_2_out, S1, not_1_out);
  not not_1 (not_1_out, S0);
  and and_5 (and_5_out, S1, Z_q, ZERO);
  or or_3 (or_3_out, and_5_out, and_6_out, and_7_out);
  and and_6 (and_6_out, ZERO, SP_prime);
  and and_7 (and_7_out, S0, ZERO);
  J_K_Flip_Flop X (.J(and_1_out), .clk(CLK), .K(and_1_out), .Q(S1));  // open: Qn, preset, en, reset
  J_K_Flip_Flop Y (.J(or_1_out), .clk(CLK), .K(and_4_out), .Q(S0));  // open: Qn, preset, en, reset
  J_K_Flip_Flop Z (.J(or_2_out), .clk(CLK), .K(or_3_out), .Q(Z_q));  // open: Qn, preset, en, reset
  not not_2 (TS, S0);
  not not_3 (LOAD, Z_q);
  and and_8 (SE, S1, TS, Z_q);
endmodule

module Decodificador_de_Salidas (
  input  S1,
  input  S0,
  output LRV,
  output LAV,
  output LVV,
  output LRP,
  output LVP
);

  wire not_1_out, not_2_out;

  not not_1 (not_1_out, S0);
  not not_2 (not_2_out, S1);
  and and_1 (LAV, not_2_out, S0);
  and and_2 (LVV, not_2_out, not_1_out);
  or or_1 (LRP, not_2_out, S0);
  and and_3 (LVP, S1, not_1_out);

  assign LRV = S1;
endmodule

module Modulo_de_Tiempos (
  input  CLK,
  input  EN,
  input  SET,
  input  RESET,
  input  LOAD,
  input  TS,
  output [3:0] MSB_top,
  output [3:0] LSB_top,
  output [2:0] MSB_bot,
  output [2:0] LSB_bot,
  output ZERO
);

  wire [5:0] estado_1_out_6, multiplexer_1_out, multiplexer_2_out, multiplexer_3_out, previo_1_out,
       siguiente_1_out;

  Multiplexer #(.width(6), .enable("false")) multiplexer_1 (
    .in0(previo_1_out), .in1(siguiente_1_out), .out(multiplexer_1_out), .sel(1'b0));
  Multiplexer #(.width(6), .enable("false")) multiplexer_2 (
    .in0(multiplexer_1_out), .in1(multiplexer_3_out), .out(multiplexer_2_out), .sel(LOAD));
  Multiplexer #(.width(6), .enable("false")) multiplexer_3 (
    .in0(6'b101000), .in1(6'b001010), .out(multiplexer_3_out), .sel(TS));
  estado estado_1 (.CLK(CLK), .D(multiplexer_2_out), .S(SET), .EN(EN), .R(RESET), .out_6(estado_1_out_6));
  previo previo_1 (.IN(estado_1_out_6), .OUT(previo_1_out));
  siguiente siguiente_1 (.IN(estado_1_out_6), .OUT(siguiente_1_out));
  _6bit2bcd_main main_1 (
    .in_1(estado_1_out_6), .MSB_top(MSB_top), .LSB_top(LSB_top), .MSB_bot(MSB_bot), .LSB_bot(LSB_bot));
  zero_max zero_max_1 (.in_1(estado_1_out_6), .ZERO(ZERO));  // open: MAX
  _7_Segment_Display u_7_segment_display_1 (
    .g(MSB_top[0]), .f(MSB_top[1]), .a(MSB_top[2]), .b(MSB_top[3]), .e(MSB_bot[2]), .d(MSB_bot[1]),
    .c(MSB_bot[0]));  // open: dp
  _7_Segment_Display u_7_segment_display_2 (
    .g(LSB_top[0]), .f(LSB_top[1]), .a(LSB_top[2]), .b(LSB_top[3]), .e(LSB_bot[2]), .d(LSB_bot[1]),
    .c(LSB_bot[0]));  // open: dp
endmodule

module Solicitud_de_Paso (
  input  SP,
  input  CLK,
  input  RES,
  input  LVP,
  output SP_prime
);

  wire or_1_out;

  S_R_Flip_Flop s_r_ff_1 (.S(1'b0), .clk(CLK), .R(1'b0), .Q(SP_prime), .preset(SP), .reset(or_1_out));  // open: Qn, en
  or or_1 (or_1_out, RES, LVP);
endmodule
